# Fritzing sketch practica2 (saved by Fritzing 0.9.1b)
breadboards: 1

parts:
  Parte1 = Arduino Uno (Rev3)
  S1 = Reed switch [package=THT]
  LED1 = smd LED [color="Red (633nm)" package="0805 [SMD]"]
  J1 = Piezo Speaker
  R1 = Resistor [tolerance=±5% resistance=220 package=THT]
  R2 = Trimmer Potentiometer [maximum_resistance=10kΩ package=THT]
  U1 = LCD-16X2 [package=lcd-16x2_noholes]

nets:
  N1: Parte1.D8, U1.RS
  N2: Parte1.D9_PWM, U1.E
  N3: Parte1.D10_PWM/SS, J1.pin2
  GND: Parte1.GND, S1.pin_2, LED1.cathode, J1.pin1, R2.leg1, U1.VSS, U1.R_W, U1.K
  N4: Parte1.D2, R1.Pin_0
  N5: Parte1.D3_PWM, S1.pin_1
  N6: Parte1.D4, U1.DB4
  N7: Parte1.D5_PWM, U1.DB5
  N8: Parte1.D6_PWM, U1.DB6
  N9: Parte1.D7, U1.DB7
  5V: Parte1.5V, R2.wiper, R2.leg2, U1.VDD, U1.A
  N10: LED1.anode, R1.Pin_1
